# Fritzing sketch smart_bar (saved by Fritzing 0.9.0b)
circuit board: 4cm x 6cm
breadboards: 1

parts:
  R1 = Resistor [tolerance=±5% resistance=200 package=THT]
  BTN1 = Pushbutton [package="[THT]"]
  R2 = Resistor [tolerance=±5% resistance=1k package=THT]
  R3 = Resistor [tolerance=±5% resistance=10k package=THT]
  U1 = atmega328 [package=dip]
  Q1 = NPN-Transistor [package="TO92 [THT]"]
  SJ2 = Screw terminal - 3 pins [package=THT]
  PJ1 = Screw terminal - 2 pins [package=THT]
  BATT1 = 3xAAA Switchable Battery Pack w/JST connector
  E18-D80NK = PIR sensor
  OLED1 = 128x64 Monochrom OLED Display with SPI Control
  J1 = Piezo Speaker

nets (from the schematic view):
  N1: R1.Pin_0, R3.Pin_1, U1.GND#7
  N2: R1.Pin_1, J1.pin1
  N3: BTN1.Pin_1, BTN1.Pin_2, U1.D2
  N4: BTN1.Pin_3, BTN1.Pin_4, R3.Pin_0
  N5: R2.Pin_0, U1.D7
  N6: R2.Pin_1, Q1.B
  N7: U1.D1_(TX), J1.pin2
  N8: U1.D3_(PWM), OLED1.SCL
  N9: U1.D4, OLED1.SDA
  VCC: U1.VCC, SJ2.pin1, PJ1.pin1, BATT1.POS, E18-D80NK.VDD
  N10: U1.D5_(PWM), OLED1.RST
  N11: U1.D6_(PWM), OLED1.D/C
  N12: U1.D8, SJ2.pin2, E18-D80NK.SIG
  N13: Q1.E, PJ1.pin2, BATT1.NEG, OLED1.GND
  N14: Q1.C, SJ2.pin3, E18-D80NK.GND

notes:
  VCC
  SIG
  GND
  +
  -

custom parts:
  NPN-Transistor: A standard NPN-transistor
  Screw terminal - 3 pins: Screw terminal with 3 pins
  Screw terminal - 2 pins: Screw terminal with 2 pins
  3xAAA Switchable Battery Pack w/JST connector: 3xAAA Switchable Battery Pack with JST connector
  Piezo Speaker: Piezo

// code stored in the sketch: ultrasonic_and_lcd.ino
/*
 HC-SR04 Ping distance sensor]
 VCC to arduino 5v GND to arduino GND
 Echo to Arduino pin 13 Trig to Arduino pin 12
 Red POS to Arduino pin 11
 Green POS to Arduino pin 10
 560 ohm resistor to both LED NEG and GRD power rail
 More info at: http://goo.gl/kJ8Gl
 Original code improvements to the Ping sketch sourced from Trollmaker.com
 Some code and wiring inspired by http://en.wikiversity.org/wiki/User:Dstaub/robotcar
 */

// include the library code:
#include <LiquidCrystal.h>
#include <ve_avr.h>

// initialize the library with the numbers of the interface pins
LiquidCrystal lcd(0, 1, 2, 3, 4, 5);

// (1)Рисуем букву Ш
byte Sh_kr_lit[8] =
{
  B10001,
  B10001,
  B10101,
  B10101,
  B10101,
  B10101,
  B11111,
  B00000,
};
// (2)Рисуем букву З
byte Z_kr_lit[8] =
{
  B01110,
  B10001,
  B00001,
  B00110,
  B00001,
  B10001,
  B01110,
  B00000,
};
// (3)Рисуем букву У
byte U_kr_lit[8] =
{
  B10001,
  B10001,
  B10001,
  B01111,
  B00010,
  B00100,
  B11000,
  B00000,
};
// (4)Рисуем букву Л
byte L_kr_lit[8] =
{
  B00111,
  B01001,
  B01001,
  B01001,
  B01001,
  B01001,
  B10001,
  B00000,
};
// (5)Рисуем букву Ь
byte MZ_kr_lit[8] =
{
  B10000,
  B10000,
  B10000,
  B11110,
  B10001,
  B10001,
  B11110,
  B00000,
};
// (6)Рисуем букву П
byte P_kr_lit[8] =
{
  B11111,
  B10001,
  B10001,
  B10001,
  B10001,
  B10001,
  B10001,
  B00000,
};
// (7)Рисуем букву И
byte I_kr_lit[8] =
{
  B10001,
  B10001,
  B10001,
  B10011,
  B10101,
  B11001,
  B10001,
  B00000,
};

#define trigPin 13
#define echoPin 12
#define led 10

unsigned long iNoSensitivityTime=1000;//время нечувствительности к прерыванию сенсора
float distanceNoSensitiveRatio= 0.2;
long timeBeforeSleep= 30000;
long delayTime= 200;
long objectDistance=50;

int iResult= 0;
unsigned long iLastSwitchTime=0;
long lastDistance=0;
unsigned long sleepTimer=0;
unsigned long sleepTimerZero=0;
boolean just_woke_up=true;

void printHello() 
{
  lcd.clear();
// Устанавливаем курсор в 1-й столбец 1-й строки. Нумерация идёт с нуля, сначала столбец
  lcd.setCursor(0, 0);
// Выводим на дисплей "ВАШ РЕЗУЛЬТАТ:"
  lcd.print("\6P\7BET!");
}

void printYourResult() 
{
// Устанавливаем курсор в 1-й столбец 1-й строки. Нумерация идёт с нуля, сначала столбец
  lcd.setCursor(0, 0);
// Выводим на дисплей "ВАШ РЕЗУЛЬТАТ:"
  lcd.print("BA\1 PE\2\3\4\5TAT:");
}

void printValue(int value2print) 
{
// Устанавливаем курсор в 1-й столбец 1-й строки. Нумерация идёт с нуля, сначала столбец
  lcd.setCursor(0, 1);
// Выводим на дисплей значение
  lcd.print(value2print);
}

void printGoodBye() 
{
  lcd.clear();
// Устанавливаем курсор в 1-й столбец 1-й строки. Нумерация идёт с нуля, сначала столбец
  lcd.setCursor(0, 0);
  lcd.print("\6OKA!");
  delay(1000);
  lcd.noDisplay();
}
#define LCD_LIGHT_PIN A4
void setup() {
 
  pinMode(trigPin, OUTPUT);
  pinMode(echoPin, INPUT);
  pinMode(led, OUTPUT);
  
  lcd.createChar(1, Sh_kr_lit);// Создаем собственный символ номер 1 - ш
  lcd.createChar(2, Z_kr_lit);// Создаем собственный символ номер 2 - з
  lcd.createChar(3, U_kr_lit);// Создаем собственный символ номер 3 - у
  lcd.createChar(4, L_kr_lit);// Создаем собственный символ номер 4 - у
  lcd.createChar(5, MZ_kr_lit);// Создаем собственный символ номер 5 - ь
  lcd.createChar(6, P_kr_lit);// Создаем собственный символ номер 6 - п
  lcd.createChar(7, I_kr_lit);// Создаем собственный символ номер 7 - и
// Инициализируем дисплей: 2 строки по 16 символов
  lcd.begin(16, 2);
  
  pinMode(LCD_LIGHT_PIN, OUTPUT);
  // Set the lcd display backlight anode pin to low - lcd light off.
  digitalWrite(LCD_LIGHT_PIN, HIGH);
  
  printHello();
  
  DEV_POWER.adcOff();       // Выключение АЦП (analogRead)
  DEV_POWER.usart0Off();    // Выключение USART (Serial)
  DEV_POWER.spiOff();       // Выключение SPI
  DEV_POWER.twiOff();       // Выключение TWI (Wire)
  DEV_SLEEP.setMode(SleepControl::IDLE);  // Выбор режима сна
  DEV_SLEEP.enableSleep();                    // Разрешить переход в спящий режим
                                 
}

boolean bLockResult= false;

void loop() {

  long duration, distance;

  digitalWrite(trigPin, LOW);  // Added this line
  delayMicroseconds(2); // Added this line
  digitalWrite(trigPin, HIGH);
  delayMicroseconds(10); // Added this line
  digitalWrite(trigPin, LOW);
  duration = pulseIn(echoPin, HIGH);
  distance = (duration/2) / 29.1;

  unsigned long timeNow=millis();
  if (distance < objectDistance) {  // This is where the LED On/Off happens
  
    if(just_woke_up==true)
    {
       sleepTimer=0; 
       sleepTimerZero=millis();
       bLockResult= false;
       lastDistance=0;
       lcd.clear();
       lcd.display();
       iResult=0;
       iLastSwitchTime=0;
       printYourResult();
       printValue(iResult);
       digitalWrite(LCD_LIGHT_PIN, HIGH);
       just_woke_up=false;
    }
        
    float distanceDelta= 0;
    if(distance>=lastDistance)
    {
        distanceDelta=float(distance)-float(lastDistance);
    }
    else
    {
        distanceDelta=float(lastDistance)-float(distance);
    }
    float distanceNoSensitiveDelta=float(distance)*distanceNoSensitiveRatio;
    if(bLockResult==false && (timeNow>=(iLastSwitchTime+iNoSensitivityTime)) && (distanceDelta>distanceNoSensitiveDelta))
    {
        digitalWrite(led,HIGH);
        iResult++;
        printValue(iResult);
        /*
        //отладка срабатывания
        String sResult= String(iResult);
        String sDistance= String(distance);
        sDistance=sResult+"("+sDistance+")";
        lcd.print(sDistance);
        //конец отладки срабатывания
        */
        bLockResult= true;
        iLastSwitchTime=timeNow;
        sleepTimer=0; 
        sleepTimerZero=millis();
        
    }
    else
    {
      digitalWrite(led,LOW);
    }
  }
  else {
    digitalWrite(led,LOW);
    bLockResult= false;
    /*
    //отладка срабатывания
    String sDistance= String(distance);
    sDistance="("+sDistance;
    sDistance+=")";
    lcd.setCursor(0, 1);
    lcd.print(sDistance);
    //конец отладки срабатывания
    */
  }
  lastDistance= distance;

  
  if(sleepTimer>timeBeforeSleep)
  {
    just_woke_up=true;
    printGoodBye();
    digitalWrite(LCD_LIGHT_PIN, LOW);
    sleep();
  }
  sleepTimer=millis()-sleepTimerZero; 
  delay(delayTime);
  
}
